# Fritzing sketch Lab06 Prelab Schematic (saved by Fritzing 0.9.0b)
breadboards: 1

parts:
  Launchpad1 = TI Launchpad MSP430G2
  DRIVER = H-Bridge [package=THT]
  REGULATOR = Voltage Regulator [package=to-220-alt]
  RIGHT_MOTOR = DC Motor
  LEFT_MOTOR = DC Motor
  V2 = DC Power [voltage=5]
  V3 = DC Power [voltage=5]
  V4 = DC Power [voltage=5]
  SENSOR = AD22100 - Voltage Output Temperature Sensor with Signal Conditioning [part_number=AD22100]

nets:
  N1: Launchpad1.p9, DRIVER.3A
  N2: Launchpad1.p8, DRIVER.4A
  N3: Launchpad1.p4, DRIVER.1A
  N4: Launchpad1.p3, DRIVER.2A
  N5: Launchpad1.p11, REGULATOR.OUT, SENSOR.V+
  N6: Launchpad1.p14, SENSOR.Vo
  GND: Launchpad1.p19, DRIVER.GND1, DRIVER.GND2, DRIVER.GND3, DRIVER.GND4, REGULATOR.GND, V4.V-, SENSOR.GND
  5V: DRIVER.1_2EN, DRIVER.3_4EN, DRIVER.VCC1, REGULATOR.IN
  N7: DRIVER.1Y, LEFT_MOTOR.pin_1
  N8: DRIVER.2Y, LEFT_MOTOR.pin_2
  N9: DRIVER.VCC2, V2.V+
  N10: DRIVER.3Y, RIGHT_MOTOR.pin_2
  N11: DRIVER.4Y, RIGHT_MOTOR.pin_1
  N12: V2.V-, V3.V+
  N13: V3.V-, V4.V+
